# Fritzing sketch connection (saved by Fritzing 0.9.3b)
breadboards: 1

parts:
  Squix1 = OLED 0.96" 128x64 I2C SSD1306
  J1 = STM32 Nucleo boards
  R1 = Resistor [tolerance=±5% resistance=4.7k package=THT]
  R2 = Resistor [tolerance=±5% resistance=4.7k package=THT]

nets:
  VCC: Squix1.VCC, J1.3V3, R1.Pin_0
  GND: Squix1.GND, J1.GND
  N1: Squix1.SCL, J1.A5/SCL, R1.Pin_1
  N2: Squix1.SCA, J1.A4/SDA, R2.Pin_1
